// Logisim project Safe lock.circ as structural Verilog: 5 circuits, main circuit main
module main (
);

  wire _0_out, _1_out, _2_out, _3_out, _4_out, _5_out, _6_out, _7_out, _8_out, _9_out, clock_1_out,
       key_detector_2_1_out_3, last_2_1_out_5, led_controler_1_out_3, priority_encoder_1_gs;
  wire [3:0] priority_encoder_1_out, store_1_out_4, store_1_out_5, store_1_out_6, store_1_out_7;

  Button _1 (.out(_1_out));
  Button _4 (.out(_4_out));
  Button _7 (.out(_7_out));
  Clock clock_1 (.out(clock_1_out));
  Button _2 (.out(_2_out));
  Button _5 (.out(_5_out));
  Button _8 (.out(_8_out));
  Button _0 (.out(_0_out));
  Button _3 (.out(_3_out));
  Button _6 (.out(_6_out));
  Button _9 (.out(_9_out));
  Priority_Encoder #(.select(4)) priority_encoder_1 (
    .in0(_0_out), .in1(_1_out), .in2(_2_out), .in3(_3_out), .in4(_4_out), .in5(_5_out), .in6(_6_out),
    .in7(_7_out), .in8(_8_out), .in9(_9_out), .out(priority_encoder_1_out), .gs(priority_encoder_1_gs));  // open: in10, in11, in12, in13, in14, in15, en_out, en_in
  key_detector_2 key_detector_2_1 (.in_1(priority_encoder_1_gs), .in_2(clock_1_out), .out_3(key_detector_2_1_out_3));
  store store_1 (
    .in_1(priority_encoder_1_out), .in_2(clock_1_out), .out_4(store_1_out_4), .out_5(store_1_out_5),
    .out_6(store_1_out_6), .out_7(store_1_out_7), .in_3(key_detector_2_1_out_3));
  last_2 last_2_1 (
    .in_1(store_1_out_7), .in_2(store_1_out_6), .in_3(store_1_out_5), .in_4(store_1_out_4),
    .out_5(last_2_1_out_5));
  led_controler led_controler_1 (.in_2(clock_1_out), .in_1(last_2_1_out_5), .out_3(led_controler_1_out_3));
  LED led_1 (.in(led_controler_1_out_3));
endmodule

module store (
  input  [3:0] in_1,
  input  in_2,
  input  in_3,
  output [3:0] out_4,
  output [3:0] out_5,
  output [3:0] out_6,
  output [3:0] out_7
);

  Register #(.width(4)) register_1 (.D(in_1), .en(in_3), .Q(out_4), .clk(in_2));  // open: clr
  Register #(.width(4)) register_2 (.D(out_4), .en(in_3), .Q(out_5), .clk(in_2));  // open: clr
  Register #(.width(4)) register_3 (.D(out_5), .en(in_3), .Q(out_6), .clk(in_2));  // open: clr
  Register #(.width(4)) register_4 (.D(out_6), .en(in_3), .Q(out_7), .clk(in_2));  // open: clr
endmodule

module key_detector_2 (
  input  in_1,
  input  in_2,
  output out_3
);

  wire and_1_out, and_2_out, and_3_out, d_ff_1_q, d_ff_1_qn, d_ff_2_qn, or_1_out;

  and and_1 (and_1_out, d_ff_1_q, in_1);
  and and_2 (and_2_out, in_1, out_3);
  or or_1 (or_1_out, and_1_out, and_2_out);
  and and_3 (and_3_out, d_ff_1_qn, in_1, d_ff_2_qn);
  D_Flip_Flop d_ff_1 (.clk(in_2), .D(or_1_out), .Q(d_ff_1_q), .Qn(d_ff_1_qn));  // open: preset, en, reset
  D_Flip_Flop d_ff_2 (.clk(in_2), .D(and_3_out), .Q(out_3), .Qn(d_ff_2_qn));  // open: preset, en, reset
endmodule

module last_2 (
  input  [3:0] in_1,
  input  [3:0] in_2,
  input  [3:0] in_3,
  input  [3:0] in_4,
  output out_5
);

  wire comparator_1_eq, comparator_2_eq, comparator_3_eq, comparator_4_eq;

  Comparator #(.width(4)) comparator_1 (.a(4'b0000), .b(in_1), .eq(comparator_1_eq));  // open: gt, lt
  Comparator #(.width(4)) comparator_2 (.a(4'b0110), .b(in_2), .eq(comparator_2_eq));  // open: gt, lt
  Comparator #(.width(4)) comparator_3 (.a(4'b0000), .b(in_3), .eq(comparator_3_eq));  // open: gt, lt
  Comparator #(.width(4)) comparator_4 (.a(4'b0110), .b(in_4), .eq(comparator_4_eq));  // open: gt, lt
  and and_1 (out_5, comparator_1_eq, comparator_2_eq, comparator_3_eq, comparator_4_eq);
endmodule

module led_controler (
  input  in_1,
  input  in_2,
  output out_3
);

  wire and_1_out, comparator_1_eq, comparator_1_gt, comparator_2_eq, comparator_2_gt, comparator_3_gt,
       comparator_3_lt, not_1_out, or_1_out, or_2_out, or_3_out;
  wire [9:0] counter_1_q;

  not not_1 (not_1_out, in_1);
  and and_1 (and_1_out, in_1, or_1_out);
  Counter #(.width(10), .max('h3ff)) counter_1 (
    .count(and_1_out), .Q(counter_1_q), .clk(in_2), .clr(not_1_out));  // open: load, D, carry
  or or_1 (or_1_out, comparator_1_gt, comparator_1_eq);
  Comparator #(.width(10)) comparator_1 (
    .a(counter_1_q), .b(10'h3e8), .gt(comparator_1_gt), .eq(comparator_1_eq));  // open: lt
  Comparator #(.width(10)) comparator_2 (
    .a(counter_1_q), .b(10'h3e8), .gt(comparator_2_gt), .eq(comparator_2_eq));  // open: lt
  Comparator #(.width(10)) comparator_3 (
    .a(counter_1_q), .b({10{1'b0}}), .gt(comparator_3_gt), .lt(comparator_3_lt));  // open: eq
  or or_2 (or_2_out, comparator_2_gt, comparator_2_eq);
  or or_3 (or_3_out, comparator_3_gt, comparator_3_lt);
  and and_2 (out_3, or_2_out, or_3_out);
endmodule
