// Logisim project bcd adder.circ as structural Verilog: 2 circuits, main circuit main
module main (
  input  in_1,
  input  in_2,
  input  in_3,
  input  in_4,
  input  in_5,
  input  in_6,
  input  in_7,
  input  in_8,
  input  in_9,
  input  in_10,
  input  in_11,
  input  in_12,
  input  in_13,
  input  in_14,
  input  in_15,
  input  in_16,
  input  in_17,
  input  in_18,
  input  in_19,
  input  in_20,
  input  in_21,
  input  in_22,
  input  in_23,
  input  in_24,
  input  in_25,
  input  in_26,
  input  in_27,
  input  in_28,
  input  in_29,
  input  in_30,
  input  in_31,
  input  in_32,
  output out_33,
  output out_34,
  output out_35,
  output out_36,
  output out_37,
  output out_38,
  output out_39,
  output out_40,
  output out_41,
  output out_42,
  output out_43,
  output out_44,
  output out_45,
  output out_46,
  output out_47,
  output out_48,
  output out_49
);

  wire adder_1_cout, adder_1_out, adder_2_cout, adder_2_out, adder_3_cout, adder_4_cout, adder_4_out,
       adder_5_cout, adder_6_cout, adder_6_out, adder_7_cout, adder_8_cout, adder_9_cout, adder_9_out,
       adder_10_cout, adder_11_cout, adder_11_out, adder_12_cout, adder_12_out, adder_13_cout, adder_14_cout,
       adder_14_out, adder_15_cout, adder_16_cout, adder_16_out, adder_17_cout, adder_18_cout, adder_18_out,
       adder_19_cout, adder_20_cout, adder_20_out, adder_21_cout, adder_22_cout, adder_22_out, adder_23_cout,
       adder_24_cout, adder_25_cout, adder_25_out, adder_26_cout, adder_27_cout, adder_27_out, adder_28_cout,
       adder_28_out, adder_29_cout, adder_30_cout, adder_30_out, adder_31_cout, adder_32_cout, and_1_out,
       and_2_out, and_3_out, and_4_out, and_5_out, and_6_out, and_7_out, and_8_out, or_2_out, or_3_out,
       or_4_out, or_5_out, or_6_out, or_7_out, or_8_out;

  or or_1 (out_33, adder_1_cout, adder_3_cout);
  Adder #(.width(1)) adder_1 (.a(in_17), .b(in_1), .out(adder_1_out), .cin(adder_2_cout), .cout(adder_1_cout));
  Adder #(.width(1)) adder_2 (.a(in_21), .b(in_2), .out(adder_2_out), .cin(adder_4_cout), .cout(adder_2_cout));
  Adder #(.width(1)) adder_3 (.a(1'b0), .b(adder_1_out), .out(out_34), .cin(adder_5_cout), .cout(adder_3_cout));
  Adder #(.width(1)) adder_4 (.a(in_22), .b(in_3), .out(adder_4_out), .cin(adder_6_cout), .cout(adder_4_cout));
  or or_2 (or_2_out, adder_1_cout, and_1_out, and_2_out);
  Adder #(.width(1)) adder_5 (.a(or_2_out), .b(adder_2_out), .out(out_35), .cin(adder_7_cout), .cout(adder_5_cout));
  Hex_Digit_Display hex_digit_display_1 (.value({in_1, in_2, in_3, in_4}));  // open: dp
  Hex_Digit_Display hex_digit_display_2 (.value({in_17, in_21, in_22, in_23}));  // open: dp
  Adder #(.width(1)) adder_6 (.a(in_23), .b(in_4), .out(adder_6_out), .cin(or_3_out), .cout(adder_6_cout));
  and and_1 (and_1_out, adder_4_out, adder_1_out);
  and and_2 (and_2_out, adder_2_out, adder_1_out);
  Adder #(.width(1)) adder_7 (.a(or_2_out), .b(adder_4_out), .out(out_36), .cin(adder_8_cout), .cout(adder_7_cout));
  or or_3 (or_3_out, adder_9_cout, adder_10_cout);
  Adder #(.width(1)) adder_8 (.a(1'b0), .b(adder_6_out), .out(out_37), .cin(1'b0), .cout(adder_8_cout));
  Adder #(.width(1)) adder_9 (.a(in_18), .b(in_5), .out(adder_9_out), .cin(adder_11_cout), .cout(adder_9_cout));
  Adder #(.width(1)) adder_10 (.a(1'b0), .b(adder_9_out), .out(out_38), .cin(adder_13_cout), .cout(adder_10_cout));
  Adder #(.width(1)) adder_11 (.a(in_24), .b(in_6), .out(adder_11_out), .cin(adder_12_cout), .cout(adder_11_cout));
  or or_4 (or_4_out, adder_9_cout, and_3_out, and_4_out);
  Adder #(.width(1)) adder_12 (.a(in_25), .b(in_7), .out(adder_12_out), .cin(adder_14_cout), .cout(adder_12_cout));
  and and_3 (and_3_out, adder_12_out, adder_9_out);
  and and_4 (and_4_out, adder_11_out, adder_9_out);
  Adder #(.width(1)) adder_13 (.a(or_4_out), .b(adder_11_out), .out(out_39), .cin(adder_15_cout), .cout(adder_13_cout));
  Hex_Digit_Display hex_digit_display_3 (.value({in_5, in_6, in_7, in_8}));  // open: dp
  Hex_Digit_Display hex_digit_display_4 (.value({in_18, in_24, in_25, in_26}));  // open: dp
  Adder #(.width(1)) adder_14 (.a(in_26), .b(in_8), .out(adder_14_out), .cin(or_5_out), .cout(adder_14_cout));
  or or_5 (or_5_out, adder_16_cout, adder_19_cout);
  Adder #(.width(1)) adder_15 (.a(or_4_out), .b(adder_12_out), .out(out_40), .cin(adder_17_cout), .cout(adder_15_cout));
  Adder #(.width(1)) adder_16 (.a(in_19), .b(in_9), .out(adder_16_out), .cin(adder_18_cout), .cout(adder_16_cout));
  Adder #(.width(1)) adder_17 (.a(1'b0), .b(adder_14_out), .out(out_41), .cin(1'b0), .cout(adder_17_cout));
  Adder #(.width(1)) adder_18 (.a(in_27), .b(in_10), .out(adder_18_out), .cin(adder_20_cout), .cout(adder_18_cout));
  Adder #(.width(1)) adder_19 (.a(1'b0), .b(adder_16_out), .out(out_42), .cin(adder_21_cout), .cout(adder_19_cout));
  Adder #(.width(1)) adder_20 (.a(in_28), .b(in_11), .out(adder_20_out), .cin(adder_22_cout), .cout(adder_20_cout));
  or or_6 (or_6_out, adder_16_cout, and_5_out, and_6_out);
  Adder #(.width(1)) adder_21 (.a(or_6_out), .b(adder_18_out), .out(out_43), .cin(adder_23_cout), .cout(adder_21_cout));
  Hex_Digit_Display hex_digit_display_5 (.value({out_34, out_35, out_36, out_37}));  // open: dp
  Hex_Digit_Display hex_digit_display_6 (.value({in_9, in_10, in_11, in_12}));  // open: dp
  Hex_Digit_Display hex_digit_display_7 (.value({in_19, in_27, in_28, in_29}));  // open: dp
  Adder #(.width(1)) adder_22 (.a(in_29), .b(in_12), .out(adder_22_out), .cin(or_7_out), .cout(adder_22_cout));
  and and_5 (and_5_out, adder_20_out, adder_16_out);
  and and_6 (and_6_out, adder_16_out, adder_18_out);
  Adder #(.width(1)) adder_23 (.a(or_6_out), .b(adder_20_out), .out(out_44), .cin(adder_24_cout), .cout(adder_23_cout));
  Hex_Digit_Display hex_digit_display_8 (.value({out_38, out_39, out_40, out_41}));  // open: dp
  Hex_Digit_Display hex_digit_display_9 (.value({out_42, out_43, out_44, out_45}));  // open: dp
  or or_7 (or_7_out, adder_25_cout, adder_26_cout);
  Adder #(.width(1)) adder_24 (.a(1'b0), .b(adder_22_out), .out(out_45), .cin(1'b0), .cout(adder_24_cout));
  Hex_Digit_Display hex_digit_display_10 (.value({out_46, out_47, out_48, out_49}));  // open: dp
  Adder #(.width(1)) adder_25 (.a(in_20), .b(in_13), .out(adder_25_out), .cin(adder_27_cout), .cout(adder_25_cout));
  Adder #(.width(1)) adder_26 (.a(1'b0), .b(adder_25_out), .out(out_46), .cin(adder_29_cout), .cout(adder_26_cout));
  Adder #(.width(1)) adder_27 (.a(in_30), .b(in_14), .out(adder_27_out), .cin(adder_28_cout), .cout(adder_27_cout));
  Adder #(.width(1)) adder_28 (.a(in_31), .b(in_15), .out(adder_28_out), .cin(adder_30_cout), .cout(adder_28_cout));
  Adder #(.width(1)) adder_29 (.a(or_8_out), .b(adder_27_out), .out(out_47), .cin(adder_31_cout), .cout(adder_29_cout));
  Hex_Digit_Display hex_digit_display_11 (.value({in_13, in_14, in_15, in_16}));  // open: dp
  Hex_Digit_Display hex_digit_display_12 (.value({in_20, in_30, in_31, in_32}));  // open: dp
  Adder #(.width(1)) adder_30 (.a(in_32), .b(in_16), .out(adder_30_out), .cin(1'b0), .cout(adder_30_cout));
  or or_8 (or_8_out, and_7_out, and_8_out, adder_25_cout);
  Adder #(.width(1)) adder_31 (.a(or_8_out), .b(adder_28_out), .out(out_48), .cin(adder_32_cout), .cout(adder_31_cout));
  and and_7 (and_7_out, adder_28_out, adder_25_out);
  and and_8 (and_8_out, adder_25_out, adder_27_out);
  Adder #(.width(1)) adder_32 (.a(1'b0), .b(adder_30_out), .out(out_49), .cin(1'b0), .cout(adder_32_cout));
endmodule

module BCD_ADDER (
  input  a4,
  input  a1,
  input  a2,
  input  a3,
  input  b1,
  input  b2,
  input  b3,
  input  b4,
  input  c_in,
  output c_out,
  output s1,
  output s2,
  output s3,
  output s4
);

  wire adder_1_cout, adder_1_out, adder_2_cout, adder_2_out, adder_3_cout, adder_4_cout, adder_4_out,
       adder_5_cout, adder_6_cout, adder_6_out, adder_7_cout, adder_8_cout, and_1_out, and_2_out, or_2_out;

  or or_1 (c_out, adder_1_cout, adder_3_cout);
  Adder #(.width(1)) adder_1 (.a(b1), .b(a1), .out(adder_1_out), .cin(adder_2_cout), .cout(adder_1_cout));
  Adder #(.width(1)) adder_2 (.a(b2), .b(a2), .out(adder_2_out), .cin(adder_4_cout), .cout(adder_2_cout));
  Adder #(.width(1)) adder_3 (.a(1'b0), .b(adder_1_out), .out(s1), .cin(adder_5_cout), .cout(adder_3_cout));
  Adder #(.width(1)) adder_4 (.a(b3), .b(a3), .out(adder_4_out), .cin(adder_6_cout), .cout(adder_4_cout));
  Adder #(.width(1)) adder_5 (.a(or_2_out), .b(adder_2_out), .out(s2), .cin(adder_7_cout), .cout(adder_5_cout));
  Adder #(.width(1)) adder_6 (.a(b4), .b(a4), .out(adder_6_out), .cin(c_in), .cout(adder_6_cout));
  Adder #(.width(1)) adder_7 (.a(or_2_out), .b(adder_4_out), .out(s3), .cin(adder_8_cout), .cout(adder_7_cout));
  and and_1 (and_1_out, adder_4_out, adder_1_out);
  or or_2 (or_2_out, and_1_out, and_2_out, adder_1_cout);
  and and_2 (and_2_out, adder_1_out, adder_2_out);
  Adder #(.width(1)) adder_8 (.a(1'b0), .b(adder_6_out), .out(s4), .cin(1'b0), .cout(adder_8_cout));
endmodule
