// Logisim project binary Subtract.circ as structural Verilog: 1 circuit, main circuit main
module main (
  input  [3:0] in_1,
  input  [3:0] in_2,
  input  [3:0] in_3,
  input  [3:0] in_4,
  output [3:0] out_5,
  output [3:0] out_6
);

  wire adder_2_cout, not_1_out, not_3_out, not_5_out;
  wire [3:0] controlled_buffer_1_out, controlled_buffer_3_out, not_2_out, not_4_out, or_1_out;

  assign controlled_buffer_1_out = not_1_out ? in_4 : 4'bz;  // Controlled_Buffer controlled_buffer_1
  not not_1 (not_1_out, not_3_out);
  assign not_2_out = ~out_6;  // NOT_Gate not_2, 4 bits wide
  assign controlled_buffer_1_out = not_3_out ? out_5 : 4'bz;  // Controlled_Buffer controlled_buffer_2
  Adder #(.width(4)) adder_1 (.a(not_2_out), .b(4'b0000), .out(out_5), .cin(1'b1));  // open: cout
  not not_3 (not_3_out, adder_2_cout);
  assign or_1_out = controlled_buffer_1_out | controlled_buffer_3_out;  // OR_Gate or_1, 4 bits wide
  assign not_4_out = ~in_2;  // NOT_Gate not_4, 4 bits wide
  assign controlled_buffer_3_out = adder_2_cout ? out_6 : 4'bz;  // Controlled_Buffer controlled_buffer_3
  assign controlled_buffer_3_out = not_5_out ? in_3 : 4'bz;  // Controlled_Buffer controlled_buffer_4
  not not_5 (not_5_out, adder_2_cout);
  Adder #(.width(4)) adder_2 (.a(not_4_out), .b(in_1), .out(out_6), .cin(1'b1), .cout(adder_2_cout));
  Hex_Digit_Display hex_digit_display_1 (.value(in_1));  // open: dp
  Hex_Digit_Display hex_digit_display_2 (.value(in_2));  // open: dp
  _7_Segment_Display u_7_segment_display_1 (.g(not_3_out));  // open: f, a, b, e, d, c, dp
  Hex_Digit_Display hex_digit_display_3 (.value(or_1_out));  // open: dp
  _7_Segment_Display u_7_segment_display_2 (.g(1'b1));  // open: f, a, b, e, d, c, dp
endmodule
