// Logisim project binary sum.circ as structural Verilog: 1 circuit, main circuit main
module main (
  input  in_1,
  input  in_2,
  input  in_3,
  input  A,
  input  in_5,
  input  in_6,
  input  in_7,
  input  in_8,
  input  B,
  output out_10,
  output out_11,
  output out_12,
  output out_13,
  output C_out
);

  wire and_1_out, and_2_out, and_3_out, and_4_out, and_5_out, and_6_out, and_7_out, and_8_out, or_1_out,
       or_3_out, or_4_out, xor_1_out, xor_2_out, xor_5_out, xor_6_out;

  xor xor_1 (xor_1_out, in_2, in_7);
  and and_1 (and_1_out, in_7, in_2);
  xor xor_2 (xor_2_out, in_5, in_6);
  and and_2 (and_2_out, in_6, in_5);
  and and_3 (and_3_out, or_4_out, xor_1_out);
  xor xor_3 (out_10, xor_1_out, or_4_out);
  or or_1 (or_1_out, and_3_out, and_1_out);
  xor xor_4 (out_11, xor_2_out, or_1_out);
  and and_4 (and_4_out, or_1_out, xor_2_out);
  or or_2 (C_out, and_4_out, and_2_out);
  xor xor_5 (xor_5_out, A, B);
  and and_5 (and_5_out, B, A);
  xor xor_6 (xor_6_out, in_3, in_8);
  and and_6 (and_6_out, in_8, in_3);
  xor xor_7 (out_12, xor_5_out, in_1);
  and and_7 (and_7_out, in_1, xor_5_out);
  xor xor_8 (out_13, xor_6_out, or_3_out);
  and and_8 (and_8_out, or_3_out, xor_6_out);
  or or_3 (or_3_out, and_7_out, and_5_out);
  or or_4 (or_4_out, and_8_out, and_6_out);
endmodule
