// Logisim project coffee machine.circ as structural Verilog: 2 circuits, main circuit main
module main (
);

  wire mansour_1__1, mansour_1__2, mansour_1__3, mansour_1__4, mansour_1__5, mansour_1__6, mansour_1__7,
       mansour_1__8, mansour_1__9;
  wire [3:0] mansour_1_return_money, undriven, vending_keypad_1_p1;

  // Vending_Keypad vending_keypad_1: pin names not known; wires that end beside it: vending_keypad_1_p1
  Hex_Digit_Display hex_digit_display_1 (.value(undriven));  // open: dp
  // Money_Counter money_counter_1: pin names not known
  mansour mansour_1 (
    .return_money(mansour_1_return_money), ._1(mansour_1__1), ._2(mansour_1__2), ._3(mansour_1__3),
    ._4(mansour_1__4), ._5(mansour_1__5), ._6(mansour_1__6), ._7(mansour_1__7), ._8(mansour_1__8),
    ._9(mansour_1__9), .select_item(vending_keypad_1_p1), .input_money(undriven));
  // Money_Returner money_returner_1: pin names not known; wires that end beside it: mansour_1_return_money
  LED _1nis (.in(mansour_1__1));
  LED _1nis_2 (.in(mansour_1__4));
  LED _2nis (.in(mansour_1__7));
  LED _2nis_2 (.in(mansour_1__2));
  LED _1nis_3 (.in(mansour_1__5));
  LED _2nis_3 (.in(mansour_1__8));
  LED _3nis (.in(mansour_1__3));
  LED _1nis_4 (.in(mansour_1__6));
  LED _2nis_4 (.in(mansour_1__9));
endmodule

module mansour (
  input  [3:0] select_item,
  input  [3:0] input_money,
  output [3:0] return_money,
  output _1,
  output _2,
  output _3,
  output _4,
  output _5,
  output _6,
  output _7,
  output _8,
  output _9
);

  wire not_1_out, subtractor_1_bout;
  wire [3:0] multiplexer_1_out, subtractor_1_out;

  Multiplexer #(.select(4), .width(4)) multiplexer_1 (
    .in0(4'b0000), .in1(4'b0001), .in2(4'b0010), .in3(4'b0011), .in4(4'b0001), .in5(4'b0001), .in6(4'b0001),
    .in7(4'b0010), .in8(4'b0010), .in9(4'b0010), .in10(4'b0000), .in11(4'b0000), .in12(4'b0000),
    .in13(4'b0000), .in14(4'b0000), .in15(4'b0000), .out(multiplexer_1_out), .sel(select_item));  // open: en
  Decoder #(.select(4), .disabled(0)) decoder_1 (
    .out1(_1), .out2(_2), .out3(_3), .out4(_4), .out5(_5), .out6(_6), .out7(_7), .out8(_8), .out9(_9),
    .sel(select_item), .en(not_1_out));  // open: out0, out10, out11, out12, out13, out14, out15
  Subtractor #(.width(4)) subtractor_1 (
    .a(input_money), .b(multiplexer_1_out), .out(subtractor_1_out), .bin(1'b0), .bout(subtractor_1_bout));
  not not_1 (not_1_out, subtractor_1_bout);
  assign return_money = not_1_out ? subtractor_1_out : 4'bz;  // Controlled_Buffer controlled_buffer_1
endmodule
