// Logisim project trafic lights.circ as structural Verilog: 1 circuit, main circuit main
module main (
);

  wire and_1_out, and_2_out, and_3_out, clock_1_out, d_ff_1_qn, d_ff_2_qn, d_ff_3_q, d_ff_3_qn,
       decoder_1_out0, decoder_1_out1, decoder_1_out2, or_1_out;
  wire [1:0] d_ff_2_q;

  and and_1 (and_1_out, d_ff_2_q[1], d_ff_2_qn, d_ff_3_q);
  and and_2 (and_2_out, d_ff_1_qn, d_ff_2_q[0], d_ff_3_qn);
  or or_1 (or_1_out, and_1_out, and_2_out);
  and and_3 (and_3_out, d_ff_2_q[0], d_ff_3_qn, d_ff_1_qn);
  Clock clock_1 (.out(clock_1_out));
  D_Flip_Flop d_ff_1 (.clk(clock_1_out), .D(and_3_out), .Q(d_ff_2_q[1]), .Qn(d_ff_1_qn));  // open: preset, en, reset
  D_Flip_Flop d_ff_2 (.clk(clock_1_out), .D(d_ff_2_qn), .Q(d_ff_2_q[0]), .Qn(d_ff_2_qn));  // open: preset, en, reset
  D_Flip_Flop d_ff_3 (.clk(clock_1_out), .D(or_1_out), .Q(d_ff_3_q), .Qn(d_ff_3_qn));  // open: preset, en, reset
  Decoder #(.select(2)) decoder_1 (
    .out0(decoder_1_out0), .out1(decoder_1_out1), .out2(decoder_1_out2), .sel(d_ff_2_q));  // open: out3, en
  LED led_1 (.in(decoder_1_out0));
  LED led_2 (.in(decoder_1_out1));
  LED led_3 (.in(decoder_1_out2));
endmodule
